# Fritzing sketch Color Sensor Project (saved by Fritzing 0.9.9b)

parts:
  Part1 = Arduino Nano (Rev3.0) (ICSP)
  J1 = Basic Servo
  Part2 = LCD1602-I2C
  e-radionica1 = TCS230 Color Sensor [part_number=101209]

nets:
  N1: Part1.D4, e-radionica1.S0
  N2: Part1.D5, e-radionica1.S1
  N3: Part1.D6, e-radionica1.S2
  N4: Part1.D7, e-radionica1.S3
  N5: Part1.D8, e-radionica1.Out
  N6: Part1.A5, Part2.SCL
  N7: Part1.A4, Part2.SDA
  GND: J1.gnd, Part2.GND, e-radionica1.Gnd
  VCC: J1.vcc, Part2.VCC, e-radionica1.Vcc

custom parts:
  LCD1602-I2C: A standard character display, usually with 2x16 characters. Comes in many colors with LCM1602 IIC attached.
  TCS230 Color Sensor: TCS230
